// Logisim project 13BitPC.circ as structural Verilog: 1 circuit, main circuit RAM2
module RAM2 (
  input  [7:0] in_1,
  output [7:0] out_2,
  output [7:0] out_3
);

  wire and_1_out, clock_1_out, decoder_1_out5, dipswitch_1_p1, dipswitch_3_sw1, dipswitch_3_sw2,
       dipswitch_3_sw3, dipswitch_3_sw4, dipswitch_3_sw5, dipswitch_3_sw6, not_1_out;
  wire [2:0] counter_2_q;
  wire [3:0] bit_extender_1_out, counter_1_q, register_2_q, register_3_q;
  wire [6:0] dipswitch_2_sw1;
  wire [6:3] register_5_q;
  wire [7:0] adder_1_out, bit_extender_2_out, bit_extender_3_out, register_1_q, register_4_q;
  wire [12:0] rom_1_data;

  Clock clock_1 (.out(clock_1_out));
  not not_1 (not_1_out, rom_1_data[0]);
  Register register_1 (.D(out_2), .en(rom_1_data[7]), .clk(and_1_out), .Q(register_1_q), .clr(dipswitch_3_sw4));
  // DipSwitch dipswitch_1: pin names not known; wires that end beside it: dipswitch_1_p1, dipswitch_1_p1
  and and_1 (and_1_out, clock_1_out, not_1_out);
  assign out_2 = rom_1_data[6] ? register_1_q : 8'bz;  // Controlled_Buffer controlled_buffer_1
  DipSwitch #(.number(7)) dipswitch_2 (
    .sw1(dipswitch_2_sw1[0]), .sw2(dipswitch_2_sw1[1]), .sw3(dipswitch_2_sw1[2]), .sw4(dipswitch_2_sw1[3]),
    .sw5(dipswitch_2_sw1[4]), .sw6(dipswitch_2_sw1[5]), .sw7(dipswitch_2_sw1[6]));
  ROM #(.addrWidth(7), .dataWidth(13)) rom_1 (.addr({register_5_q, counter_2_q}), .data(rom_1_data));
  Register #(.width(4)) register_2 (
    .D(bit_extender_1_out), .en(rom_1_data[12]), .clk(and_1_out), .Q(register_2_q), .clr(dipswitch_3_sw6));
  Bit_Extender #(.out_width(4), .\type ("zero")) bit_extender_1 (.in(out_2), .out(bit_extender_1_out));
  RAM #(.addrWidth(4), .trigger("falling")) ram_1 (
    .addr(register_2_q), .we(rom_1_data[10]), .oe(not_1_out), .clk(and_1_out), .din(out_2), .dout(out_3));
  Register #(.width(4)) register_3 (
    .D(out_2[3:0]), .en(rom_1_data[3]), .clk(and_1_out), .Q(register_3_q), .clr(dipswitch_3_sw5));
  assign out_2 = rom_1_data[1] ? register_4_q : 8'bz;  // Controlled_Buffer controlled_buffer_2
  Register register_4 (.D(out_2), .en(rom_1_data[2]), .clk(and_1_out), .Q(register_4_q), .clr(dipswitch_3_sw1));
  assign out_2 = rom_1_data[4] ? out_3 : 8'bz;  // Controlled_Buffer controlled_buffer_3
  Register #(.width(4)) register_5 (
    .D(out_2[7:4]), .en(rom_1_data[3]), .clk(and_1_out), .Q(register_5_q), .clr(dipswitch_3_sw3));
  assign out_2 = rom_1_data[11] ? bit_extender_2_out : 8'bz;  // Controlled_Buffer controlled_buffer_4
  assign out_2 = rom_1_data[5] ? adder_1_out : 8'bz;  // Controlled_Buffer controlled_buffer_5
  Adder adder_1 (.a(register_1_q), .b(register_4_q), .out(adder_1_out));  // open: cin, cout
  Counter #(.max('hf), .width(4)) counter_1 (
    .clr(dipswitch_3_sw2), .clk(rom_1_data[8]), .Q(counter_1_q));  // open: load, up, count, D, carry
  Counter #(.max('h7), .trigger("falling"), .width(3)) counter_2 (
    .clr(decoder_1_out5), .clk(and_1_out), .Q(counter_2_q));  // open: load, up, count, D, carry
  assign out_2 = rom_1_data[9] ? bit_extender_3_out : 8'bz;  // Controlled_Buffer controlled_buffer_6
  assign bit_extender_2_out = {{4{1'b0}}, register_3_q};  // Bit_Extender bit_extender_2
  Decoder #(.select(3)) decoder_1 (
    .out5(decoder_1_out5), .sel(counter_2_q));  // open: out0, out1, out2, out3, out4, out6, out7, en
  assign bit_extender_3_out = {{4{1'b0}}, counter_1_q};  // Bit_Extender bit_extender_3
  DipSwitch dipswitch_3 (
    .sw1(dipswitch_3_sw1), .sw2(dipswitch_3_sw2), .sw3(dipswitch_3_sw3), .sw4(dipswitch_3_sw4),
    .sw5(dipswitch_3_sw5), .sw6(dipswitch_3_sw6));  // open: sw7, sw8

  // Notes on the sheet:
  //   A
  //   contents of rom_1 (hex, n*v repeats v):
  //   1200 118 6*0 1200 118 1800 90 4*0 1200 118 1800 24 4*0 1200 118 6*0 1200 118 1800 440 4*0 1200 118
  //   880 5*0 1200 118 6*0 1200 118 6*0 1200 118 6*0 1200 118 6*0 1200 118 6*0 1200 118 6*0 1200 118 6*0
  //   1200 118 6*0 1200 118 6*0 8*1
  //   BUS
  //   Adress Register
  //   B
  //   MI
  //   IO
  //   RI
  //   PCO
  //   PCE
  //   Instruction register
  //   AI
  //   AO
  //   ADDER
  //   ADO
  //   RO
  //   II
  //   BI
  //   BO
  //   Program counter
  //   Mini step counter
  //   HLT
endmodule
