// Logisim project 8BitPC.circ as structural Verilog: 1 circuit, main circuit RAM2
module RAM2 (
  input  [7:0] in_1,
  output [7:0] out_2,
  output [7:0] out_3
);

  wire and_1_out, and_2_out, clock_1_out, decoder_1_out5, dipswitch_1_p1, dipswitch_1_p2, dipswitch_3_sw1,
       dipswitch_3_sw2, dipswitch_3_sw3, dipswitch_3_sw4, dipswitch_3_sw5, dipswitch_3_sw6, dipswitch_3_sw7,
       dipswitch_3_sw8, not_1_out, or_1_out;
  wire [1:0] pla_1_out;
  wire [2:0] counter_2_q;
  wire [3:0] bit_extender_1_out, bit_extender_2_out, counter_1_q, register_2_q, register_3_q;
  wire [7:0] adder_1_out, bit_extender_3_out, bit_extender_4_out, register_1_q, register_4_q;
  wire [8:0] dipswitch_2_sw9;
  wire [8:3] register_6_q;
  wire [15:0] rom_1_data;

  Clock clock_1 (.out(clock_1_out));
  not not_1 (not_1_out, rom_1_data[0]);
  Register register_1 (.D(out_2), .en(rom_1_data[7]), .clk(and_1_out), .Q(register_1_q), .clr(dipswitch_3_sw4));
  // DipSwitch dipswitch_1: pin names not known; wires that end beside it: dipswitch_1_p1, dipswitch_1_p2, dipswitch_1_p2
  and and_1 (and_1_out, clock_1_out, not_1_out);
  assign out_2 = rom_1_data[6] ? register_1_q : 8'bz;  // Controlled_Buffer controlled_buffer_1
  DipSwitch #(.number(9)) dipswitch_2 (
    .sw1(dipswitch_2_sw9[8]), .sw2(dipswitch_2_sw9[7]), .sw3(dipswitch_2_sw9[6]), .sw4(dipswitch_2_sw9[5]),
    .sw5(dipswitch_2_sw9[4]), .sw6(dipswitch_2_sw9[3]), .sw7(dipswitch_2_sw9[2]), .sw8(dipswitch_2_sw9[1]),
    .sw9(dipswitch_2_sw9[0]));
  ROM #(.addrWidth(9), .dataWidth(16)) rom_1 (.addr({register_6_q, counter_2_q}), .data(rom_1_data));
  Register #(.width(4)) register_2 (
    .D(bit_extender_1_out), .en(rom_1_data[12]), .clk(and_1_out), .Q(register_2_q), .clr(dipswitch_3_sw6));
  Bit_Extender #(.out_width(4), .\type ("zero")) bit_extender_1 (.in(out_2), .out(bit_extender_1_out));
  RAM #(.addrWidth(4), .trigger("falling")) ram_1 (
    .addr(register_2_q), .we(rom_1_data[10]), .oe(not_1_out), .clk(and_1_out), .din(out_2), .dout(out_3));
  Register #(.width(4)) register_3 (
    .D(out_2[3:0]), .en(rom_1_data[3]), .clk(and_1_out), .Q(register_3_q), .clr(dipswitch_3_sw5));
  assign out_2 = rom_1_data[1] ? register_4_q : 8'bz;  // Controlled_Buffer controlled_buffer_2
  Register register_4 (.D(out_2), .en(rom_1_data[2]), .clk(and_1_out), .Q(register_4_q), .clr(dipswitch_3_sw1));
  assign out_2 = rom_1_data[4] ? out_3 : 8'bz;  // Controlled_Buffer controlled_buffer_3
  Register #(.width(4)) register_5 (
    .D(out_2[7:4]), .en(rom_1_data[3]), .clk(and_1_out), .Q(register_6_q[6:3]), .clr(dipswitch_3_sw3));
  Bit_Extender #(.out_width(4)) bit_extender_2 (.in(out_2), .out(bit_extender_2_out));
  and and_2 (and_2_out, rom_1_data[15], and_1_out);
  or or_1 (or_1_out, and_2_out, rom_1_data[8]);
  assign out_2 = rom_1_data[11] ? bit_extender_3_out : 8'bz;  // Controlled_Buffer controlled_buffer_4
  assign out_2 = rom_1_data[5] ? adder_1_out : 8'bz;  // Controlled_Buffer controlled_buffer_5
  Adder adder_1 (.a(register_1_q), .b(register_4_q), .out(adder_1_out), .cout(pla_1_out[1]));  // open: cin
  Counter #(.max('hf), .width(4)) counter_1 (
    .clr(dipswitch_3_sw2), .load(rom_1_data[15]), .clk(or_1_out), .D(bit_extender_2_out), .Q(counter_1_q));  // open: up, count, carry
  Counter #(.max('h7), .trigger("falling"), .width(3)) counter_2 (
    .clr(decoder_1_out5), .clk(and_1_out), .Q(counter_2_q));  // open: load, up, count, D, carry
  assign out_2 = rom_1_data[9] ? bit_extender_4_out : 8'bz;  // Controlled_Buffer controlled_buffer_6
  assign bit_extender_3_out = {{4{1'b0}}, register_3_q};  // Bit_Extender bit_extender_3
  Decoder #(.select(3)) decoder_1 (
    .out5(decoder_1_out5), .sel(counter_2_q));  // open: out0, out1, out2, out3, out4, out6, out7, en
  assign bit_extender_4_out = {{4{1'b0}}, counter_1_q};  // Bit_Extender bit_extender_4
  DipSwitch dipswitch_3 (
    .sw1(dipswitch_3_sw1), .sw2(dipswitch_3_sw2), .sw3(dipswitch_3_sw3), .sw4(dipswitch_3_sw4),
    .sw5(dipswitch_3_sw5), .sw6(dipswitch_3_sw6), .sw7(dipswitch_3_sw7), .sw8(dipswitch_3_sw8));
  Register #(.width(2)) register_6 (
    .D(pla_1_out), .en(rom_1_data[14]), .clk(and_1_out), .Q(register_6_q[8:7]), .clr(dipswitch_3_sw7));
  Register register_7 (.D(out_2), .en(rom_1_data[13]), .clk(and_1_out), .clr(dipswitch_3_sw8));  // open: Q
  PLA #(.in_width(8), .out_width(1), .\table ("00000000 1")) pla_1 (.in(adder_1_out), .out(pla_1_out[0]));

  // Notes on the sheet:
  //   A
  //   contents of rom_1 (hex, n*v repeats v):
  //   1200 118 6*0 1200 118 1800 90 4*0 1200 118 1800 24 4000 0 0 0 1200 118 6*0 1200 118 1800 440 4*0
  //   1200 118 880 5*0 1200 118 8800 5*0 1200 118 6*0 1200 118 6*0 1200 118 6*0 1200 118 6*0 1200 118 6*0
  //   1200 118 6*0 1200 118 6*0 1200 118 6*0 8*1 1200 118 6*0 1200 118 1800 90 4*0 1200 118 1800 24 4000
  //   11*0 1200 118 1800 440 4*0 1200 118 880 5*0 1200 118 8800 5*0 1200 118 8800 5*0 1200 118 8800 5*0
  //   1200 118 6*0 1200 118 6*0 1200 118 6*0 1200 118 6*0 1200 118 6*0 1200 118 6*0 4*1 4*0 1200 118 6*0
  //   1200 118 1800 90 4*0 1200 118 1800 24 4000 0 0 0 1200 118 6*0 1200 118 1800 440 4*0 1200 118 880 5*0
  //   1200 118 8800 5*0 1200 118 8800 5*0 1200 118 8800 13*0 1200 118 14*0 1200 118 14*0 1200 118 6*0 4*1
  //   4*0 1200 118 6*0 1200 118 0 90 4*0 1200 118 1800 24 4000 11*0 1200 118 1800 440 4*0 1200 118 880 5*0
  //   1200 118 8800 69*0 4*1
  //   BUS
  //   Adress Register
  //   B
  //   MI
  //   FI
  //   OI
  //   PCI
  //   IO
  //   RI
  //   PCO
  //   Instruction register
  //   PCE
  //   AI
  //   ADDER
  //   AO
  //   ADO
  //   II
  //   BI
  //   RO
  //   Program counter
  //   Mini step counter
  //   HLT
  //   BO
  //   Flags Register
  //   Output register
endmodule
